// Logisim project exp3-1 d触发器(v2.7.1) - 作答区.circ as structural Verilog: 3 circuits, main circuit main
module main (
  output D,
  output EN,
  output CLK,
  output Q,
  output QN,
  output halt
);

  wire clock_1_out;
  wire [2:2] counter_1_q;

  Counter #(.width(3), .max('h7)) counter_1 (
    .Q({counter_1_q[2], D, CLK}), .carry(halt), .clk(clock_1_out));  // open: load, D, count, clr
  Clock clock_1 (.out(clock_1_out));
  D_flipflop d_flipflop_1 (.D(D), .EN(1'b1), .CLK(CLK), .Q(Q), .QN(QN));
  LED led_1 (.in(Q));
  LED led_2 (.in(QN));

  assign EN = 1'b1;

  // Notes on the sheet:
  //   顶层模块与自制子模块连接部分
  //   本地Logisim验证区域
  //   按Control+K触发执行，再次按Control+K暂停触发
endmodule

module D_latch (
  input  D,
  input  C,
  output Q,
  output QN
);

  wire nand_1_out, nand_2_out, not_1_out, not_2_out, not_3_out, not_4_out, not_5_out;

  not not_1 (not_1_out, D);
  nand nand_1 (nand_1_out, D, C);
  nand nand_2 (nand_2_out, C, not_1_out);
  not not_2 (not_2_out, nand_1_out);
  not not_3 (not_3_out, QN);
  not not_4 (not_4_out, Q);
  not not_5 (not_5_out, nand_2_out);
  or or_1 (Q, not_2_out, not_3_out);
  or or_2 (QN, not_4_out, not_5_out);

  // Notes on the sheet:
  //   D锁存器子模块实现区域
endmodule

module D_flipflop (
  input  D,
  input  EN,
  input  CLK,
  output Q,
  output QN
);

  wire and_1_out, and_2_out, d_latch_1_q, not_1_out, not_2_out, not_3_out, or_1_out;

  and and_1 (and_1_out, D, EN);
  not not_1 (not_1_out, EN);
  and and_2 (and_2_out, not_1_out, Q);
  or or_1 (or_1_out, and_1_out, and_2_out);
  not not_2 (not_2_out, CLK);
  D_latch d_latch_1 (.D(or_1_out), .C(not_2_out), .Q(d_latch_1_q));  // open: QN
  not not_3 (not_3_out, not_2_out);
  D_latch d_latch_2 (.D(d_latch_1_q), .C(not_3_out), .Q(Q), .QN(QN));

  // Notes on the sheet:
  //   D触发器子模块实现区域
endmodule
