// Logisim project exp3-3 移位寄存器(v2.7.1) - 作答区.circ as structural Verilog: 2 circuits, main circuit main
module main (
  output CLK,
  output CLR,
  output LIN,
  output RIN,
  output S1,
  output S0,
  output A,
  output B,
  output C,
  output D,
  output QA,
  output QB,
  output QC,
  output QD,
  output halt
);

  wire [3:0] bit_extender_1_out;
  wire [4:0] counter_1_q;
  wire [15:9] rom_1_data;

  Clock clock_1 (.out(CLK));
  Counter #(.width(5), .max('h1f)) counter_1 (.Q(counter_1_q), .carry(halt), .clk(CLK));  // open: load, D, count, clr
  Bit_Extender #(.in_width(5), .out_width(4)) bit_extender_1 (.in(counter_1_q), .out(bit_extender_1_out));
  ROM #(.addrWidth(4), .dataWidth(16)) rom_1 (
    .addr(bit_extender_1_out), .data({rom_1_data, CLR, LIN, RIN, S1, S0, A, B, C, D}));  // open: sel
  \_4位移位寄存器  \u_4位移位寄存器_1  (
    .CLK(CLK), .CLR(CLR), .LIN(LIN), .RIN(RIN), .S1(S1), .S0(S0), .D(D), .C(C), .B(B), .A(A), .QD(QD),
    .QC(QC), .QB(QB), .QA(QA));
  DotMatrix #(.matrixcols(4), .matrixrows(1)) dotmatrix_1 (.col0(QA), .col1(QB), .col2(QC), .col3(QD));

  // Other names for the same wires on the sheet: A_t = QA; B_t = QB; C_t = QC; D_t = QD

  // Notes on the sheet:
  //   contents of rom_1 (hex, n*v repeats v):
  //   100 35 5f 50 55 5a 90 1f 15f 3a af a0 a5 aa 60 2f
  //   顶层模块与自制子模块连接部分
  //   本地Logisim验证区域
  //   按Control+K触发执行，再次按Control+K暂停触发
endmodule

module \_4位移位寄存器  (
  input  CLK,
  input  CLR,
  input  LIN,
  input  RIN,
  input  S1,
  input  S0,
  input  D,
  input  C,
  input  B,
  input  A,
  output QD,
  output QC,
  output QB,
  output QA
);

  wire and_1_out, and_2_out, and_3_out, and_4_out, and_5_out, and_6_out, and_7_out, and_8_out, and_9_out,
       and_10_out, and_11_out, and_12_out, and_13_out, and_14_out, and_15_out, and_16_out, not_1_out,
       not_2_out, not_3_out, not_4_out, not_5_out, not_6_out, or_1_out, or_2_out, or_3_out, or_4_out;

  not not_1 (not_1_out, CLK);
  not not_2 (not_2_out, CLR);
  not not_3 (not_3_out, S1);
  not not_4 (not_4_out, S0);
  not not_5 (not_5_out, not_3_out);
  not not_6 (not_6_out, not_4_out);
  and and_1 (and_1_out, not_2_out, LIN, not_5_out, not_4_out);
  and and_2 (and_2_out, not_2_out, QD, not_3_out, not_4_out);
  and and_3 (and_3_out, not_2_out, D, not_5_out, not_6_out);
  and and_4 (and_4_out, not_2_out, QC, not_3_out, not_6_out);
  and and_5 (and_5_out, not_2_out, QD, not_5_out, not_4_out);
  and and_6 (and_6_out, not_2_out, QC, not_3_out, not_4_out);
  and and_7 (and_7_out, not_2_out, C, not_5_out, not_6_out);
  and and_8 (and_8_out, not_2_out, QB, not_3_out, not_6_out);
  and and_9 (and_9_out, not_2_out, QC, not_5_out, not_4_out);
  and and_10 (and_10_out, not_2_out, QB, not_3_out, not_4_out);
  and and_11 (and_11_out, not_2_out, B, not_5_out, not_6_out);
  and and_12 (and_12_out, not_2_out, QA, not_3_out, not_6_out);
  and and_13 (and_13_out, not_2_out, QB, not_5_out, not_4_out);
  and and_14 (and_14_out, not_2_out, QA, not_3_out, not_4_out);
  and and_15 (and_15_out, not_2_out, A, not_5_out, not_6_out);
  and and_16 (and_16_out, not_2_out, RIN, not_3_out, not_6_out);
  or or_1 (or_1_out, and_1_out, and_2_out, and_3_out, and_4_out);
  or or_2 (or_2_out, and_5_out, and_6_out, and_7_out, and_8_out);
  or or_3 (or_3_out, and_9_out, and_10_out, and_11_out, and_12_out);
  or or_4 (or_4_out, and_13_out, and_14_out, and_15_out, and_16_out);
  D_Flip_Flop d_ff_1 (.clk(not_1_out), .D(or_1_out), .Q(QD));  // open: Qn, preset, en, reset
  D_Flip_Flop d_ff_2 (.clk(not_1_out), .D(or_2_out), .Q(QC));  // open: Qn, preset, en, reset
  D_Flip_Flop d_ff_3 (.clk(not_1_out), .D(or_3_out), .Q(QB));  // open: Qn, preset, en, reset
  D_Flip_Flop d_ff_4 (.clk(not_1_out), .D(or_4_out), .Q(QA));  // open: Qn, preset, en, reset

  // Notes on the sheet:
  //   4位移位寄存器子模块实现区域
endmodule
