// Logisim project exp2-1 译码器 - 作答区.circ as structural Verilog: 2 circuits, main circuit main
module main (
  output E0,
  output E1,
  output E2,
  output I0,
  output I1,
  output I2,
  output O0,
  output O1,
  output O2,
  output O3,
  output O4,
  output O5,
  output O6,
  output halt,
  output O7
);

  wire clock_1_out, pull_resistor_1_node;
  wire [2:0] priority_encoder_1_out;
  wire [3:0] bit_extender_1_out;
  wire [7:0] Y;

  Counter #(.width(6), .max('h3f)) counter_1 (
    .Q({E2, E1, E0, I2, I1, I0}), .carry(halt), .clk(clock_1_out));  // open: load, D, count, clr
  Clock clock_1 (.out(clock_1_out));
  _3_8_decoder u_3_8_decoder_1 (
    .G1(E0), .G2A_L(E1), .G2B_L(E2), .A(I0), .B(I1), .C(I2), .Y2_L(O2), .Y3_L(O3), .Y0_L(O0), .Y1_L(O1),
    .Y4_L(O4), .Y5_L(O5), .Y6_L(O6), .Y7_L(O7));
  assign Y = ~{O7, O6, O5, O4, O3, O2, O1, O0};  // NOT_Gate not_1, 8 bits wide
  Priority_Encoder priority_encoder_1 (
    .in0(Y[0]), .in1(Y[1]), .in2(Y[2]), .in3(Y[3]), .in4(Y[4]), .in5(Y[5]), .in6(Y[6]), .in7(Y[7]),
    .out(priority_encoder_1_out), .en_in(pull_resistor_1_node));  // open: gs, en_out
  Pull_Resistor #(.pull(1)) pull_resistor_1 (.node(pull_resistor_1_node));
  assign bit_extender_1_out = {{1{1'b0}}, priority_encoder_1_out};  // Bit_Extender bit_extender_1
  Hex_Digit_Display hex_digit_display_1 (.value(bit_extender_1_out));  // open: dp

  // Notes on the sheet:
  //   顶层模块与自制子模块连接部分
  //   本地Logisim验证区域
  //   按Control+K触发执行，再次按Control+K暂停触发
endmodule

// 3-8 Decoder
module _3_8_decoder (
  input  G1,
  input  G2A_L,
  input  G2B_L,
  input  A,
  input  B,
  input  C,
  output Y0_L,
  output Y1_L,
  output Y2_L,
  output Y3_L,
  output Y4_L,
  output Y5_L,
  output Y6_L,
  output Y7_L
);

  wire and_1_out, and_2_out, and_3_out, and_4_out, and_5_out, and_6_out, and_7_out, and_8_out, and_9_out,
       not_1_out, not_2_out, not_3_out, not_4_out, not_5_out, not_6_out, not_7_out, not_8_out, not_9_out,
       not_10_out;

  not not_1 (not_1_out, G1);
  not not_2 (not_2_out, not_1_out);
  not not_3 (not_3_out, G2A_L);
  not not_4 (not_4_out, G2B_L);
  and and_1 (and_1_out, not_2_out, not_3_out, not_4_out);
  not not_5 (not_5_out, A);
  not not_6 (not_6_out, B);
  not not_7 (not_7_out, C);
  not not_8 (not_8_out, not_5_out);
  not not_9 (not_9_out, not_6_out);
  not not_10 (not_10_out, not_7_out);
  and and_2 (and_2_out, not_5_out, not_6_out, not_7_out, and_1_out);
  and and_3 (and_3_out, not_8_out, not_6_out, not_7_out, and_1_out);
  and and_4 (and_4_out, not_5_out, not_9_out, not_7_out, and_1_out);
  and and_5 (and_5_out, not_8_out, not_9_out, not_7_out, and_1_out);
  and and_6 (and_6_out, not_5_out, not_6_out, not_10_out, and_1_out);
  and and_7 (and_7_out, not_8_out, not_6_out, not_10_out, and_1_out);
  and and_8 (and_8_out, not_5_out, not_9_out, not_10_out, and_1_out);
  and and_9 (and_9_out, not_8_out, not_9_out, not_10_out, and_1_out);
  not not_11 (Y0_L, and_2_out);
  not not_12 (Y1_L, and_3_out);
  not not_13 (Y2_L, and_4_out);
  not not_14 (Y3_L, and_5_out);
  not not_15 (Y4_L, and_6_out);
  not not_16 (Y5_L, and_7_out);
  not not_17 (Y6_L, and_8_out);
  not not_18 (Y7_L, and_9_out);

  // Notes on the sheet:
  //   3-8译码器子模块实现区域
endmodule
