// Logisim project exp2-3 选择器级联 - 作答区.circ as structural Verilog: 3 circuits, main circuit main
module main (
  output D0,
  output D1,
  output D2,
  output D3,
  output S0,
  output S1,
  output Y,
  output halt
);

  wire clock_1_out;

  Counter #(.width(6), .max('h3f)) counter_1 (
    .Q({S1, S0, D3, D2, D1, D0}), .carry(halt), .clk(clock_1_out));  // open: load, D, count, clr
  Clock clock_1 (.out(clock_1_out));
  _4_1_mux u_4_1_mux_1 (.D0(D0), .D1(D1), .D2(D2), .D3(D3), .S0(S0), .S1(S1), .Y(Y));
  LED led_1 (.in(Y));

  // Notes on the sheet:
  //   顶层模块与自制子模块连接部分
  //   本地Logisim验证区域
  //   按Control+K触发执行，再次按Control+K暂停触发
endmodule

module _2_1_mux (
  input  A,
  input  B,
  input  S,
  output Y
);

  wire and_1_out, and_2_out, not_1_out;

  not not_1 (not_1_out, S);
  and and_1 (and_1_out, A, not_1_out);
  and and_2 (and_2_out, S, B);
  or or_1 (Y, and_1_out, and_2_out);

  // Notes on the sheet:
  //   2选1选择器子模块实现区域
endmodule

module _4_1_mux (
  input  D0,
  input  D1,
  input  D2,
  input  D3,
  input  S0,
  input  S1,
  output Y
);

  wire n2_1_mux_1_y, n2_1_mux_2_y;

  _2_1_mux u_2_1_mux_1 (.A(D0), .B(D1), .Y(n2_1_mux_1_y), .S(S0));
  _2_1_mux u_2_1_mux_2 (.A(D2), .B(D3), .Y(n2_1_mux_2_y), .S(S0));
  _2_1_mux u_2_1_mux_3 (.A(n2_1_mux_1_y), .B(n2_1_mux_2_y), .Y(Y), .S(S1));

  // Notes on the sheet:
  //   4选1选择器子模块实现区域
endmodule
