// Logisim project exp5-2 指令和控制器1 - 作答区.circ as structural Verilog: 5 circuits, main circuit main
module main (
  output [4:0] rd,
  output [4:0] rs1,
  output [4:0] rs2,
  output [6:0] funct7,
  output Branch,
  output Jump,
  output ALUAsrc,
  output [1:0] ALUBsrc,
  output [3:0] ALUctr,
  output MemtoReg,
  output RegWr,
  output MemWr,
  output halt,
  output [2:0] ExtOp
);

  wire clk;
  wire [2:0] \指令测试_1_funct3 ;
  wire [6:0] \指令测试_1_opcode ;
  wire [9:0] Addr;
  wire [11:0] bit_extender_1_out;
  wire [31:0] Instr;

  Clock clock_1 (.out(clk));
  Counter #(.width(4), .max('hf), .trigger("falling")) counter_1 (
    .carry(halt), .clk(clk));  // open: load, D, count, Q, clr
  \指令测试  \u_指令测试_1  (
    .CLK(clk), .Jump(Jump), .Branch(Branch), .Zero(1'b1), .opcode(\指令测试_1_opcode ), .rd(rd),
    .funct3(\指令测试_1_funct3 ), .rs1(rs1), .rs2(rs2), .funct7(funct7), .ExtOp(ExtOp), .instr(Instr),
    .instr_addr(Addr));  // open: imm
  assign bit_extender_1_out = {{2{1'b0}}, Addr};  // Bit_Extender bit_extender_1
  \控制器  \u_控制器_1  (
    .op0(\指令测试_1_opcode [0]), .Branch(Branch), .op1(\指令测试_1_opcode [1]), .op2(\指令测试_1_opcode [2]),
    .op3(\指令测试_1_opcode [3]), .Jump(Jump), .op4(\指令测试_1_opcode [4]), .op5(\指令测试_1_opcode [5]),
    .MemtoReg(MemtoReg), .op6(\指令测试_1_opcode [6]), .fn0(\指令测试_1_funct3 [0]), .fn1(\指令测试_1_funct3 [1]),
    .fn2(\指令测试_1_funct3 [2]), .RegWr(RegWr), .MemWr(MemWr), .ALUctr0(ALUctr[0]), .ALUctr1(ALUctr[1]),
    .ALUctr2(ALUctr[2]), .ALUctr3(ALUctr[3]), .ALUASrc(ALUAsrc), .ALUBSrc0(ALUBsrc[0]),
    .ALUBSrc1(ALUBsrc[1]), .ExtOP0(ExtOp[0]), .ExtOP1(ExtOp[1]), .ExtOP2(ExtOp[2]));
  Hex_Digit_Display hex_digit_display_1 (.value(Instr[27:24]));  // open: dp
  Hex_Digit_Display hex_digit_display_2 (.value(Instr[31:28]));  // open: dp
  Hex_Digit_Display hex_digit_display_3 (.value(Instr[19:16]));  // open: dp
  Hex_Digit_Display hex_digit_display_4 (.value(Instr[23:20]));  // open: dp
  Hex_Digit_Display hex_digit_display_5 (.value(Instr[11:8]));  // open: dp
  Hex_Digit_Display hex_digit_display_6 (.value(Instr[15:12]));  // open: dp
  Hex_Digit_Display hex_digit_display_7 (.value(bit_extender_1_out[11:8]));  // open: dp
  Hex_Digit_Display hex_digit_display_8 (.value(Instr[3:0]));  // open: dp
  Hex_Digit_Display hex_digit_display_9 (.value(Instr[7:4]));  // open: dp
  Hex_Digit_Display hex_digit_display_10 (.value(bit_extender_1_out[7:4]));  // open: dp
  Hex_Digit_Display hex_digit_display_11 (.value(bit_extender_1_out[3:0]));  // open: dp

  // Notes on the sheet:
  //   当前执行指令原码
  //   下条指令读取地址
  //   顶层模块与自制子模块连接部分
  //   本地Logisim验证区域
  //   按Control+K触发执行，再次按Control+K暂停触发
endmodule

module \指令存储器  (
  input  [9:0] Addr,
  output [31:0] Instr
);

  ROM #(.addrWidth(10), .dataWidth(32)) rom_1 (.addr(Addr), .data(Instr));  // open: sel

  // Notes on the sheet:
  //   指令存储器子模块实现区域
  //   contents of rom_1 (hex, n*v repeats v):
  //   a004b3 20af33 20bf33 f00ef13 412483 8137 912223 7ea500e3 1015*0 818ff56f
endmodule

module \立即数扩展器件  (
  input  [31:0] Instr,
  input  [2:0] ExtOp,
  output [31:0] Imm
);

  wire [11:0] bit_extender_4_out;
  wire [19:0] bit_extender_1_out, bit_extender_2_out, bit_extender_3_out;

  assign bit_extender_1_out = {{19{Instr[31]}}, Instr[31]};  // Bit_Extender bit_extender_1
  assign bit_extender_2_out = {{19{Instr[31]}}, Instr[31]};  // Bit_Extender bit_extender_2
  assign bit_extender_3_out = {{19{Instr[31]}}, Instr[31]};  // Bit_Extender bit_extender_3
  assign bit_extender_4_out = {{11{Instr[31]}}, Instr[31]};  // Bit_Extender bit_extender_4
  Multiplexer #(.select(3), .width(32), .enable("false")) multiplexer_1 (
    .in0({bit_extender_1_out, Instr[31:20]}), .in1({Instr[31:12], {12{1'b0}}}),
    .in2({bit_extender_2_out, Instr[31:25], Instr[11:7]}),
    .in3({bit_extender_3_out, Instr[7], Instr[30:25], Instr[11:8], 1'b0}),
    .in4({bit_extender_4_out, Instr[19:12], Instr[20], Instr[30:21], 1'b0}), .in5({32{1'b0}}),
    .in6({32{1'b0}}), .in7({32{1'b0}}), .out(Imm), .sel(ExtOp));

  // Notes on the sheet:
  //   立即数扩展器件子模块实现区域
endmodule

module \控制器  (
  input  op0,
  input  op1,
  input  op2,
  input  op3,
  input  op4,
  input  op5,
  input  op6,
  input  fn0,
  input  fn1,
  input  fn2,
  output Branch,
  output Jump,
  output MemtoReg,
  output RegWr,
  output MemWr,
  output ALUctr0,
  output ALUctr1,
  output ALUctr2,
  output ALUctr3,
  output ALUASrc,
  output ALUBSrc0,
  output ALUBSrc1,
  output ExtOP0,
  output ExtOP1,
  output ExtOP2
);

  wire and_4_out, and_5_out, and_6_out, and_8_out, and_9_out, and_10_out, and_11_out, and_12_out, and_13_out,
       and_14_out, and_15_out, and_18_out, and_19_out, and_20_out, and_21_out, and_22_out, and_23_out,
       and_24_out, not_1_out, not_2_out, not_3_out, not_4_out, not_5_out, not_6_out, not_7_out, not_8_out,
       not_9_out, not_10_out, not_11_out, not_12_out, not_13_out, not_14_out, not_15_out, not_16_out,
       not_17_out, not_18_out, not_19_out, not_20_out, not_21_out, not_22_out, not_23_out, not_24_out,
       not_25_out, not_26_out, not_27_out, not_28_out, not_29_out, not_30_out, not_31_out, not_32_out,
       not_33_out, not_34_out, not_35_out, not_36_out, not_37_out, not_38_out, not_39_out, not_40_out,
       not_41_out, not_42_out, not_43_out, not_44_out, not_45_out, not_46_out, not_47_out, not_48_out,
       not_49_out, not_50_out, not_51_out, not_52_out, not_53_out, not_54_out, not_55_out, not_56_out,
       not_57_out, not_58_out, not_59_out, not_60_out, not_61_out, not_62_out, not_63_out, not_64_out,
       not_65_out, not_66_out, not_67_out, not_68_out, not_69_out, not_70_out, not_71_out, not_72_out,
       not_73_out, not_74_out, not_75_out, not_76_out, not_77_out, not_78_out;

  not not_1 (not_1_out, op2);
  not not_2 (not_2_out, op3);
  not not_3 (not_3_out, op4);
  not not_4 (not_4_out, op4);
  not not_5 (not_5_out, op2);
  not not_6 (not_6_out, op3);
  not not_7 (not_7_out, op4);
  not not_8 (not_8_out, op5);
  not not_9 (not_9_out, op6);
  not not_10 (not_10_out, op2);
  not not_11 (not_11_out, op3);
  not not_12 (not_12_out, op5);
  not not_13 (not_13_out, op6);
  not not_14 (not_14_out, op3);
  not not_15 (not_15_out, op6);
  not not_16 (not_16_out, op4);
  not not_17 (not_17_out, op2);
  not not_18 (not_18_out, op3);
  not not_19 (not_19_out, op4);
  not not_20 (not_20_out, op6);
  not not_21 (not_21_out, fn0);
  not not_22 (not_22_out, fn2);
  not not_23 (not_23_out, op2);
  not not_24 (not_24_out, op3);
  not not_25 (not_25_out, op6);
  not not_26 (not_26_out, op3);
  not not_27 (not_27_out, op6);
  not not_28 (not_28_out, op2);
  not not_29 (not_29_out, op3);
  not not_30 (not_30_out, op6);
  not not_31 (not_31_out, op3);
  not not_32 (not_32_out, op6);
  not not_33 (not_33_out, op2);
  not not_34 (not_34_out, op3);
  not not_35 (not_35_out, op6);
  not not_36 (not_36_out, op3);
  not not_37 (not_37_out, op6);
  not not_38 (not_38_out, op2);
  not not_39 (not_39_out, op3);
  not not_40 (not_40_out, op4);
  not not_41 (not_41_out, op3);
  not not_42 (not_42_out, op6);
  not not_43 (not_43_out, op4);
  not not_44 (not_44_out, op4);
  not not_45 (not_45_out, op2);
  not not_46 (not_46_out, op3);
  not not_47 (not_47_out, op4);
  not not_48 (not_48_out, op6);
  not not_49 (not_49_out, fn0);
  not not_50 (not_50_out, fn2);
  not not_51 (not_51_out, op2);
  not not_52 (not_52_out, op3);
  not not_53 (not_53_out, op5);
  not not_54 (not_54_out, op6);
  not not_55 (not_55_out, fn0);
  not not_56 (not_56_out, op3);
  not not_57 (not_57_out, op6);
  not not_58 (not_58_out, op2);
  not not_59 (not_59_out, op3);
  not not_60 (not_60_out, op4);
  not not_61 (not_61_out, fn0);
  not not_62 (not_62_out, fn1);
  not not_63 (not_63_out, fn2);
  not not_64 (not_64_out, op3);
  not not_65 (not_65_out, op6);
  not not_66 (not_66_out, op2);
  not not_67 (not_67_out, op3);
  not not_68 (not_68_out, op4);
  not not_69 (not_69_out, op6);
  not not_70 (not_70_out, fn0);
  not not_71 (not_71_out, fn2);
  not not_72 (not_72_out, op2);
  not not_73 (not_73_out, op3);
  not not_74 (not_74_out, op4);
  not not_75 (not_75_out, fn0);
  not not_76 (not_76_out, fn1);
  not not_77 (not_77_out, fn2);
  not not_78 (not_78_out, op4);
  and and_1 (Branch, op0, op1, not_1_out, not_2_out, not_3_out, op5, op6);
  and and_2 (Jump, op0, op1, op2, op3, not_4_out, op5, op6);
  and and_3 (MemtoReg, op0, op1, not_5_out, not_6_out, not_7_out, not_8_out, not_9_out);
  and and_4 (and_4_out, op0, op1, not_10_out, not_11_out, not_12_out, not_13_out);
  and and_5 (and_5_out, op0, op1, not_14_out, op4, op5, not_15_out);
  and and_6 (and_6_out, op0, op1, op2, op3, not_16_out, op5, op6);
  and and_7 (MemWr, op0, op1, not_17_out, not_18_out, not_19_out, op5, not_20_out, not_21_out, fn1, not_22_out);
  and and_8 (and_8_out, op0, op1, not_23_out, not_24_out, op4, not_25_out, fn0);
  and and_9 (and_9_out, op0, op1, op2, not_26_out, op4, op5, not_27_out);
  and and_10 (and_10_out, op0, op1, not_28_out, not_29_out, op4, not_30_out, fn1);
  and and_11 (and_11_out, op0, op1, op2, not_31_out, op4, op5, not_32_out);
  and and_12 (and_12_out, op0, op1, not_33_out, not_34_out, op4, not_35_out, fn2);
  and and_13 (and_13_out, op0, op1, op2, not_36_out, op4, op5, not_37_out);
  and and_14 (and_14_out, op0, op1, not_38_out, not_39_out, not_40_out, op5, op6);
  and and_15 (and_15_out, op0, op1, op2, not_41_out, op4, op5, not_42_out);
  and and_16 (ALUASrc, op0, op1, op2, op3, not_43_out, op5, op6);
  and and_17 (ALUBSrc0, op0, op1, op2, op3, not_44_out, op5, op6);
  and and_18 (and_18_out, op0, op1, not_45_out, not_46_out, not_47_out, not_48_out, not_49_out, fn1, not_50_out);
  and and_19 (and_19_out, op0, op1, not_51_out, not_52_out, op4, not_53_out, not_54_out, not_55_out, fn1, fn2);
  and and_20 (and_20_out, op0, op1, op2, not_56_out, op4, op5, not_57_out);
  and and_21 (and_21_out, op0, op1, not_58_out, not_59_out, not_60_out, op5, op6, not_61_out, not_62_out, not_63_out);
  and and_22 (and_22_out, op0, op1, op2, not_64_out, op4, op5, not_65_out);
  and and_23 (and_23_out, op0, op1, not_66_out, not_67_out, not_68_out, op5, not_69_out, not_70_out, fn1, not_71_out);
  and and_24 (and_24_out, op0, op1, not_72_out, not_73_out, not_74_out, op5, op6, not_75_out, not_76_out, not_77_out);
  and and_25 (ExtOP2, op0, op1, op2, op3, not_78_out, op5, op6);
  or or_1 (RegWr, and_4_out, and_5_out, and_6_out);
  or or_2 (ALUctr0, and_8_out, and_9_out);
  or or_3 (ALUctr1, and_10_out, and_11_out);
  or or_4 (ALUctr2, and_12_out, and_13_out);
  or or_5 (ALUctr3, and_14_out, and_15_out);
  or or_6 (ALUBSrc1, and_18_out, and_19_out, and_20_out);
  or or_7 (ExtOP0, and_21_out, and_22_out);
  or or_8 (ExtOP1, and_23_out, and_24_out);

  // Notes on the sheet:
  //   op4: pull=down
  //   op1: pull=down
  //   op3: pull=down
  //   fn1: pull=down
  //   op0: pull=down
  //   fn2: pull=down
  //   fn0: pull=down
  //   op6: pull=down
  //   op2: pull=down
  //   op5: pull=down
  //   控制器子模块实现区域
endmodule

module \指令测试  (
  input  CLK,
  input  Jump,
  input  Branch,
  input  Zero,
  input  [2:0] ExtOp,
  output [9:0] instr_addr,
  output [31:0] instr,
  output [6:0] opcode,
  output [4:0] rd,
  output [2:0] funct3,
  output [4:0] rs1,
  output [4:0] rs2,
  output [6:0] funct7,
  output [31:0] imm
);

  wire and_1_out, or_1_out;
  wire [31:0] adder_1_out, multiplexer_1_out, multiplexer_2_out, register_1_q;

  Multiplexer #(.width(32), .enable("false")) multiplexer_1 (
    .in0(adder_1_out), .in1(32'h190), .out(multiplexer_1_out), .sel(1'b0));
  and and_1 (and_1_out, Branch, Zero);
  Register #(.width(32)) register_1 (
    .D(multiplexer_1_out), .Q({register_1_q[31:12], instr_addr, register_1_q[1:0]}), .clk(CLK));  // open: en, clr
  Multiplexer #(.width(32), .enable("false")) multiplexer_2 (
    .in0(32'h4), .in1(imm), .out(multiplexer_2_out), .sel(or_1_out));
  or or_1 (or_1_out, Jump, and_1_out);
  Adder #(.width(32)) adder_1 (
    .a({register_1_q[31:12], instr_addr, register_1_q[1:0]}), .b(multiplexer_2_out), .out(adder_1_out));  // open: cin, cout
  \立即数扩展器件  \u_立即数扩展器件_1  (.Instr({funct7, instr[24:15], funct3, instr[11:0]}), .ExtOp(ExtOp), .Imm(imm));
  \指令存储器  \u_指令存储器_1  (.Addr(instr_addr), .Instr({funct7, instr[24:15], funct3, instr[11:0]}));

  assign {instr[31:25], instr[14:12]} = {funct7, funct3};
  assign opcode = instr[6:0];
  assign rd = instr[11:7];
  assign rs1 = instr[19:15];
  assign rs2 = instr[24:20];

  // Notes on the sheet:
  //   指令解析测试子模块实现区域
endmodule
