// Logisim project exp4-2 级联加法器(v2.7.1) - 作答区.circ as structural Verilog: 6 circuits, main circuit main
module main (
  output Cin,
  output [15:0] X,
  output halt,
  output [15:0] Y,
  output Cout,
  output [15:0] S
);

  wire [3:0] bit_extender_1_out, counter_1_q;

  Clock clock_1 (.out(Cin));
  Counter #(.width(4), .max('hf), .trigger("falling")) counter_1 (
    .Q(counter_1_q), .carry(halt), .clk(Cin));  // open: load, D, count, clr
  assign bit_extender_1_out = {{3{1'b0}}, Cin};  // Bit_Extender bit_extender_1
  ROM #(.addrWidth(4), .dataWidth(16)) rom_1 (.addr(counter_1_q), .data(X));  // open: sel
  ROM #(.addrWidth(4), .dataWidth(16)) rom_2 (.addr(counter_1_q), .data(Y));  // open: sel
  Hex_Digit_Display hex_digit_display_1 (.value(bit_extender_1_out));  // open: dp
  Hex_Digit_Display hex_digit_display_2 (.value(S[15:12]));  // open: dp
  Hex_Digit_Display hex_digit_display_3 (.value(X[15:12]));  // open: dp
  Hex_Digit_Display hex_digit_display_4 (.value(X[11:8]));  // open: dp
  Hex_Digit_Display hex_digit_display_5 (.value(S[11:8]));  // open: dp
  Hex_Digit_Display hex_digit_display_6 (.value(S[7:4]));  // open: dp
  Hex_Digit_Display hex_digit_display_7 (.value(X[3:0]));  // open: dp
  Hex_Digit_Display hex_digit_display_8 (.value(X[7:4]));  // open: dp
  Hex_Digit_Display hex_digit_display_9 (.value(S[3:0]));  // open: dp
  \_16位CLA  \u_16位cla_1  (
    .Cin(Cin), .X1(X[3:0]), .Y1(Y[3:0]), .X2(X[7:4]), .Y2(Y[7:4]), .X3(X[11:8]), .Y3(Y[11:8]), .X4(X[15:12]),
    .Y4(Y[15:12]), .S1(S[3:0]), .S2(S[7:4]), .S3(S[11:8]), .S4(S[15:12]), .Cout(Cout));
  Hex_Digit_Display hex_digit_display_10 (.value(Y[15:12]));  // open: dp
  LED led_1 (.in(Cout));
  Hex_Digit_Display hex_digit_display_11 (.value(Y[7:4]));  // open: dp
  Hex_Digit_Display hex_digit_display_12 (.value(Y[11:8]));  // open: dp
  Hex_Digit_Display hex_digit_display_13 (.value(Y[3:0]));  // open: dp

  // Notes on the sheet:
  //   =
  //   contents of rom_1 (hex, n*v repeats v):
  //   0 1111 2222 3333 4444 5555 6666 7777 8888 9999 a00a b00b c00c d00d eeee ffff
  //   contents of rom_2 (hex, n*v repeats v):
  //   aaaa ffff 101 202 303 a0a b0b c0c d0d f0f eeee dddd cccc bbbb 1 1
  //   +
  //   Cin
  //   S1
  //   X1
  //   X1
  //   S2
  //   S3
  //   顶层模块与自制子模块连接部分
  //   本地Logisim验证区域
  //   按Control+K触发执行，再次按Control+K暂停触发
  //   X1
  //   X1
  //   S4
  //   +
  //   Y1
  //   Cout
  //   Y3
  //   Y2
  //   Y4
endmodule

// FA
module \_1位全加器  (
  input  Cin,
  input  X,
  input  Y,
  output F,
  output P,
  output G
);

  xor xor_1 (F, Cin, X, Y);
  or or_1 (P, X, Y);
  and and_1 (G, X, Y);

  // Notes on the sheet:
  //   全加法器子模块实现区域
endmodule

// 4-bit CLU
module \_4位CLU  (
  input  C0,
  input  P1,
  input  G1,
  input  P2,
  input  G2,
  input  P3,
  input  G3,
  input  P4,
  input  G4,
  output C1,
  output C2,
  output C3,
  output C4
);

  wire and_1_out, and_2_out, and_3_out, and_4_out, and_5_out, and_6_out, and_7_out, and_8_out, and_9_out,
       and_10_out;

  and and_1 (and_1_out, C0, P1);
  and and_2 (and_2_out, C0, P1, P2);
  and and_3 (and_3_out, P2, G1);
  and and_4 (and_4_out, C0, P1, P2, P3);
  and and_5 (and_5_out, G1, P2, P3);
  and and_6 (and_6_out, G2, P3);
  and and_7 (and_7_out, C0, P1, P2, P3, P4);
  and and_8 (and_8_out, G1, P2, P3, P4);
  and and_9 (and_9_out, G2, P3, P4);
  and and_10 (and_10_out, P4, G3);
  or or_1 (C1, and_1_out, G1);
  or or_2 (C2, and_2_out, and_3_out, G2);
  or or_3 (C3, and_4_out, and_5_out, and_6_out, G3);
  or or_4 (C4, and_7_out, and_8_out, and_9_out, and_10_out, G4);

  // Notes on the sheet:
  //   先行进位逻辑单元子模块实现区域
endmodule

// 组间进位函数逻辑
module \组间进位函数逻辑单元  (
  input  P1,
  input  G1,
  input  P2,
  input  G2,
  input  P3,
  input  G3,
  input  P4,
  input  G4,
  output Pg,
  output Gg
);

  wire and_1_out, and_2_out, and_3_out;

  and and_1 (and_1_out, G1, G2, P3, P4);
  and and_2 (and_2_out, G2, P3, P4);
  and and_3 (and_3_out, G3, P4);
  and and_4 (Pg, P1, P2, P3, P4);
  or or_1 (Gg, and_1_out, and_2_out, and_3_out, G4);

  // Notes on the sheet:
  //   组间进位函数逻辑单元子模块实现区域
endmodule

// 4-bit CLA
module \可级联的4位CLA  (
  input  Cin,
  input  [3:0] X,
  input  [3:0] Y,
  output Pg,
  output Gg,
  output [3:0] S,
  output Cout
);

  wire \n1位全加器_1_g , \n1位全加器_1_p , \n1位全加器_2_g , \n1位全加器_2_p , \n1位全加器_3_g , \n1位全加器_3_p , \n1位全加器_4_g ,
       \n1位全加器_4_p , \n4位clu_1_c1 , \n4位clu_1_c2 , \n4位clu_1_c3 ;

  \exp4_1_先行进位加法器_v2_7_1____作答区_1位全加器  \u_1位全加器_1  (
    .Cin(Cin), .X(X[0]), .Y(Y[0]), .F(S[0]), .P(\n1位全加器_1_p ), .G(\n1位全加器_1_g ));
  \exp4_1_先行进位加法器_v2_7_1____作答区_1位全加器  \u_1位全加器_2  (
    .Cin(\n4位clu_1_c1 ), .X(X[1]), .Y(Y[1]), .F(S[1]), .P(\n1位全加器_2_p ), .G(\n1位全加器_2_g ));
  \exp4_1_先行进位加法器_v2_7_1____作答区_1位全加器  \u_1位全加器_3  (
    .Cin(\n4位clu_1_c2 ), .X(X[2]), .Y(Y[2]), .F(S[2]), .P(\n1位全加器_3_p ), .G(\n1位全加器_3_g ));
  \exp4_1_先行进位加法器_v2_7_1____作答区_1位全加器  \u_1位全加器_4  (
    .Cin(\n4位clu_1_c3 ), .X(X[3]), .Y(Y[3]), .F(S[3]), .P(\n1位全加器_4_p ), .G(\n1位全加器_4_g ));
  \exp4_1_先行进位加法器_v2_7_1____作答区_4位CLU  \u_4位clu_1  (
    .P1(\n1位全加器_1_p ), .C1(\n4位clu_1_c1 ), .C2(\n4位clu_1_c2 ), .G1(\n1位全加器_1_g ), .P2(\n1位全加器_2_p ),
    .G2(\n1位全加器_2_g ), .P3(\n1位全加器_3_p ), .G3(\n1位全加器_3_g ), .P4(\n1位全加器_4_p ), .G4(\n1位全加器_4_g ), .C0(Cin),
    .C3(\n4位clu_1_c3 ), .C4(Cout));
  \组间进位函数逻辑单元  \u_组间进位函数逻辑单元_1  (
    .P1(\n1位全加器_1_p ), .G1(\n1位全加器_1_g ), .P2(\n1位全加器_2_p ), .G2(\n1位全加器_2_g ), .P3(\n1位全加器_3_p ),
    .G3(\n1位全加器_3_g ), .P4(\n1位全加器_4_p ), .G4(\n1位全加器_4_g ), .Pg(Pg), .Gg(Gg));

  // Notes on the sheet:
  //   先行进位加法器子模块实现区域
endmodule

// 16-bit CLA
module \_16位CLA  (
  input  Cin,
  input  [3:0] X1,
  input  [3:0] Y1,
  input  [3:0] X2,
  input  [3:0] Y2,
  input  [3:0] X3,
  input  [3:0] Y3,
  input  [3:0] X4,
  input  [3:0] Y4,
  output [3:0] S1,
  output [3:0] S2,
  output [3:0] S3,
  output [3:0] S4,
  output Cout
);

  wire \n4位clu_1_c1 , \n4位clu_1_c2 , \n4位clu_1_c3 , \可级联的4位cla_1_gg , \可级联的4位cla_1_pg , \可级联的4位cla_2_gg ,
       \可级联的4位cla_2_pg , \可级联的4位cla_3_gg , \可级联的4位cla_3_pg , \可级联的4位cla_4_gg , \可级联的4位cla_4_pg ;

  \可级联的4位CLA  \u_可级联的4位cla_1  (
    .X(X1), .S(S1), .Y(Y1), .Pg(\可级联的4位cla_1_pg ), .Gg(\可级联的4位cla_1_gg ), .Cin(Cin));  // open: Cout
  \可级联的4位CLA  \u_可级联的4位cla_2  (
    .X(X2), .S(S2), .Y(Y2), .Pg(\可级联的4位cla_2_pg ), .Gg(\可级联的4位cla_2_gg ), .Cin(\n4位clu_1_c1 ));  // open: Cout
  \可级联的4位CLA  \u_可级联的4位cla_3  (
    .X(X3), .S(S3), .Y(Y3), .Pg(\可级联的4位cla_3_pg ), .Gg(\可级联的4位cla_3_gg ), .Cin(\n4位clu_1_c2 ));  // open: Cout
  \可级联的4位CLA  \u_可级联的4位cla_4  (
    .X(X4), .S(S4), .Y(Y4), .Cout(Cout), .Pg(\可级联的4位cla_4_pg ), .Gg(\可级联的4位cla_4_gg ), .Cin(\n4位clu_1_c3 ));
  \_4位CLU  \u_4位clu_1  (
    .P1(\可级联的4位cla_1_pg ), .G1(\可级联的4位cla_1_gg ), .P2(\可级联的4位cla_2_pg ), .G2(\可级联的4位cla_2_gg ),
    .P3(\可级联的4位cla_3_pg ), .G3(\可级联的4位cla_3_gg ), .P4(\可级联的4位cla_4_pg ), .G4(\可级联的4位cla_4_gg ),
    .C1(\n4位clu_1_c1 ), .C2(\n4位clu_1_c2 ), .C3(\n4位clu_1_c3 ));  // open: C0, C4

  // Notes on the sheet:
  //   16位级联先行进位加法器子模块实现区域
endmodule
